// Logisim project Semafori.circ as structural Verilog: 8 circuits, main circuit main
module main (
);

  wire _1, _2, _3, _4, Ck, CkL, counter_1_carry, G, GS, H_plus, M_plus, not_1_out, R, RES, RS, V, VS;
  wire [3:0] D, H1, H2, M1, M2, P1, P2, P3, P4, P5, P6, P7, PO1, PO2, PO3, PO4, PO5, PO6, S1, S2, S3, S4, S5,
       S6, S7, SEC1, SEC2, SO1, SO2, SO3, SO4, SO5, SO6, T1, T2, T3, T4, T5, T6, T7, TO1, TO2, TO3, TO4, TO5,
       TO6, U;

  LED led_1 (.in(R));
  LED led_2 (.in(G));
  LED led_3 (.in(V));
  Button u__1 (.out(_1));
  Button u__3 (.out(_3));
  LED led_4 (.in(RS));
  LED led_5 (.in(GS));
  LED led_6 (.in(VS));
  LED led_7 (.in(RS));
  LED led_8 (.in(GS));
  LED led_9 (.in(VS));
  LED led_10 (.in(RS));
  LED led_11 (.in(GS));
  LED led_12 (.in(VS));
  Button u__4 (.out(_4));
  LED led_13 (.in(R));
  LED led_14 (.in(G));
  LED led_15 (.in(V));
  LED led_16 (.in(RS));
  LED led_17 (.in(GS));
  LED led_18 (.in(VS));
  Button u__2 (.out(_2));
  LED led_19 (.in(R));
  LED led_20 (.in(G));
  LED led_21 (.in(V));
  LED led_22 (.in(R));
  LED led_23 (.in(G));
  LED led_24 (.in(V));
  Hex_Digit_Display hex_digit_display_1 (.value(D));  // open: dp
  Hex_Digit_Display hex_digit_display_2 (.value(U));  // open: dp
  Hex_Digit_Display hex_digit_display_3 (.value(P1));  // open: dp
  Hex_Digit_Display hex_digit_display_4 (.value(S1));  // open: dp
  Hex_Digit_Display hex_digit_display_5 (.value(T1));  // open: dp
  Hex_Digit_Display hex_digit_display_6 (.value(P2));  // open: dp
  Hex_Digit_Display hex_digit_display_7 (.value(S2));  // open: dp
  Hex_Digit_Display hex_digit_display_8 (.value(T2));  // open: dp
  Semaforo semaforo_1 (.R(R), .V(V), .G(G), .CkL(CkL));
  MemTarghe memtarghe_1 (
    .Ck(Ck), .P1(P1), .P2(P2), .P3(P3), .P4(P4), .P5(P5), .P6(P6), .P7(P7), .S1(S1), .S2(S2), .S3(S3),
    .S4(S4), .S5(S5), .S6(S6), .S7(S7), ._1(_1), ._2(_2), ._3(_3), ._4(_4), .T1(T1), .T2(T2), .T3(T3),
    .T4(T4), .T5(T5), .T6(T6), .T7(T7), .CkL(CkL));
  Hex_Digit_Display hex_digit_display_9 (.value(P4));  // open: dp
  Hex_Digit_Display hex_digit_display_10 (.value(P3));  // open: dp
  Hex_Digit_Display hex_digit_display_11 (.value(S4));  // open: dp
  Hex_Digit_Display hex_digit_display_12 (.value(S3));  // open: dp
  Hex_Digit_Display hex_digit_display_13 (.value(T3));  // open: dp
  Hex_Digit_Display hex_digit_display_14 (.value(T4));  // open: dp
  Hex_Digit_Display hex_digit_display_15 (.value(P5));  // open: dp
  Hex_Digit_Display hex_digit_display_16 (.value(P6));  // open: dp
  Hex_Digit_Display hex_digit_display_17 (.value(S5));  // open: dp
  Hex_Digit_Display hex_digit_display_18 (.value(S6));  // open: dp
  Hex_Digit_Display hex_digit_display_19 (.value(T6));  // open: dp
  Hex_Digit_Display hex_digit_display_20 (.value(T5));  // open: dp
  SemaforoSpeculare semaforospeculare_1 (.VS(VS), .GS(GS), .CkL(CkL), .RS(RS));
  Button u_M_plus (.out(M_plus));
  Button u_H_plus (.out(H_plus));
  Hex_Digit_Display hex_digit_display_21 (.value(H2));  // open: dp
  Hex_Digit_Display hex_digit_display_22 (.value(P7));  // open: dp
  Hex_Digit_Display hex_digit_display_23 (.value(S7));  // open: dp
  Hex_Digit_Display hex_digit_display_24 (.value(T7));  // open: dp
  Clock clock_1 (.out(Ck));
  Hex_Digit_Display hex_digit_display_25 (.value(H1));  // open: dp
  Hex_Digit_Display hex_digit_display_26 (.value(PO1));  // open: dp
  Hex_Digit_Display hex_digit_display_27 (.value(PO2));  // open: dp
  Hex_Digit_Display hex_digit_display_28 (.value(SO1));  // open: dp
  Hex_Digit_Display hex_digit_display_29 (.value(SO2));  // open: dp
  Hex_Digit_Display hex_digit_display_30 (.value(TO2));  // open: dp
  Hex_Digit_Display hex_digit_display_31 (.value(TO1));  // open: dp
  MemOrologio memorologio_1 (
    .Reset(RES), .P1(PO1), .S1(SO1), .T1(TO1), .P2(PO2), .S2(SO2), .T2(TO2), .P3(PO3), .S3(SO3), .T3(TO3),
    .P4(PO4), .S4(SO4), .T4(TO4), .P5(PO5), .S5(SO5), .T5(TO5), .P6(PO6), .S6(SO6), .T6(TO6), ._1(_1),
    ._2(_2), ._3(_3), ._4(_4), .M_plus(M_plus), .H_plus(H_plus), .Ck(Ck), .CkL(CkL));
  Hex_Digit_Display hex_digit_display_32 (.value(M2));  // open: dp
  Hex_Digit_Display hex_digit_display_33 (.value(M1));  // open: dp
  Hex_Digit_Display hex_digit_display_34 (.value(PO3));  // open: dp
  Hex_Digit_Display hex_digit_display_35 (.value(PO4));  // open: dp
  Hex_Digit_Display hex_digit_display_36 (.value(SO3));  // open: dp
  Hex_Digit_Display hex_digit_display_37 (.value(SO4));  // open: dp
  Hex_Digit_Display hex_digit_display_38 (.value(TO4));  // open: dp
  Hex_Digit_Display hex_digit_display_39 (.value(TO3));  // open: dp
  Multa multa_1 (._1(_1), .D(D), .U(U), ._2(_2), ._3(_3), ._4(_4), .CkL(CkL));  // open: I
  Hex_Digit_Display hex_digit_display_40 (.value(SEC2));  // open: dp
  Hex_Digit_Display hex_digit_display_41 (.value(SEC1));  // open: dp
  Hex_Digit_Display hex_digit_display_42 (.value(PO5));  // open: dp
  Hex_Digit_Display hex_digit_display_43 (.value(SO5));  // open: dp
  Hex_Digit_Display hex_digit_display_44 (.value(TO5));  // open: dp
  Button u_R (.out(RES));
  Hex_Digit_Display hex_digit_display_45 (.value(PO6));  // open: dp
  Hex_Digit_Display hex_digit_display_46 (.value(SO6));  // open: dp
  Hex_Digit_Display hex_digit_display_47 (.value(TO6));  // open: dp
  Orologio orologio_1 (
    .CkL(CkL), .Reset(RES), .M_plus(M_plus), .H_plus(H_plus), .Secondi_1(SEC1), .Secondi_2(SEC2),
    .Minuti_1(M1), .Minuti_2(M2), .Ore_1(H1), .Ore_2(H2));
  not not_1 (not_1_out, Ck);
  Counter #(.width(4), .max('h8)) counter_1 (.carry(counter_1_carry), .clk(Ck), .clr(CkL));  // open: load, D, count, Q
  and and_1 (CkL, not_1_out, counter_1_carry);

  // Notes on the sheet:
  //   RIVA ALESSANDRO
  //   A.A. 2021/2022
  //   PROGETTO DI LABORATORIO
  //   ARCHITETTURA DEGLI ELABORATORI 1
  //   1
  //   3
  //   P1
  //   P4
  //   P1
  //   P3
  //   P2
  //   SEMAFORI PEDONALI
  //   P2
  //   P3
  //   4
  //   2
  //   P4
  //   CONTATORE
  //   MULTE
  //   SEMAFORI 1- 2
  //   TARGHE
  //   GENERATORE E MEMORIZZATORE TARGHE CASUALI
  //   OROLOGIO
  //   SEMAFORI 3 - 4
  //   CLOCK
  //   16 HZ
  //   MEMORIA OROLOGIO
  //   ORARI
  //   CONTATORE E CIRCUITO MULTE
  //   U
  //   L
  //   T
  //   I
  //   M
  //   A
  //   P
  //   E
  //   N
  //   U
  //   L
  //   T
  //   I
  //   M
  //   A
  //   T
  //   E
  //   R
  //   Z
  //   U
  //   L
  //   T
  //   I
  //   M
  //   A
  //   OROLOGIO
  //   CLOCK RALLENTATO
  //   2 HZ
endmodule

module Semaforo (
  input  CkL,
  output R,
  output V,
  output G
);

  wire nand_2_out, nand_3_out, nor_1_out, Res, shift_register_1_q0, shift_register_1_q1, shift_register_1_q2,
       shift_register_1_q3, shift_register_1_q4, shift_register_1_q5, shift_register_1_q6,
       shift_register_1_q7, shift_register_1_q8, shift_register_1_q9, shift_register_1_q10,
       shift_register_1_q11, shift_register_1_q12, shift_register_1_q13, shift_register_1_q14,
       shift_register_1_q15, shift_register_1_q16, shift_register_1_q17, shift_register_1_q18,
       shift_register_1_q19;

  nand nand_1 (R, ~Res, shift_register_1_q0, shift_register_1_q1, shift_register_1_q2, shift_register_1_q3, shift_register_1_q4, shift_register_1_q5, shift_register_1_q6, shift_register_1_q7, shift_register_1_q8, shift_register_1_q9);  // NAND_Gate
  and and_1 (V, nand_2_out, ~R);  // AND_Gate
  and and_2 (G, nand_3_out, nor_1_out);
  nand nand_2 (nand_2_out, shift_register_1_q10, shift_register_1_q11, shift_register_1_q12, shift_register_1_q13);
  nand nand_3 (nand_3_out, shift_register_1_q14, shift_register_1_q15, shift_register_1_q16, shift_register_1_q17, shift_register_1_q18, shift_register_1_q19);
  nor nor_1 (nor_1_out, V, R);
  Shift_Register #(.length(20)) shift_register_1 (
    .in(1'b1), .clk(CkL), .out(Res), .clr(Res), .q0(shift_register_1_q0), .q1(shift_register_1_q1),
    .q2(shift_register_1_q2), .q3(shift_register_1_q3), .q4(shift_register_1_q4), .q5(shift_register_1_q5),
    .q6(shift_register_1_q6), .q7(shift_register_1_q7), .q8(shift_register_1_q8), .q9(shift_register_1_q9),
    .q10(shift_register_1_q10), .q11(shift_register_1_q11), .q12(shift_register_1_q12),
    .q13(shift_register_1_q13), .q14(shift_register_1_q14), .q15(shift_register_1_q15),
    .q16(shift_register_1_q16), .q17(shift_register_1_q17), .q18(shift_register_1_q18),
    .q19(shift_register_1_q19));  // open: shift, load, d0, d1, d2, d3, d4, d5, d6, d7, d8, d9, d10, d11, d12, d13, d14, d15, d16, d17, d18, d19

  // Notes on the sheet:
  //   ROSSO
  //   VERDE
  //   GIALLO
  //   CIRCUITO PER IL. FUNZIONAMENTO DEI SEMAFORI 1 E 2
endmodule

module SemaforoSpeculare (
  input  CkL,
  output VS,
  output GS,
  output RS
);

  wire G, nand_1_out, nand_2_out, not_1_out, or_1_out, R, shift_register_1_q0, shift_register_1_q1,
       shift_register_1_q2, shift_register_1_q3, shift_register_1_q4, shift_register_1_q5,
       shift_register_1_q6, shift_register_1_q7, shift_register_1_q8, shift_register_1_q9, V;

  Semaforo semaforo_1 (.R(R), .V(V), .G(G), .CkL(CkL));
  and and_1 (VS, nand_1_out, R);
  and and_2 (GS, nand_2_out, ~VS, R);  // AND_Gate
  nand nand_1 (nand_1_out, shift_register_1_q0, shift_register_1_q1, shift_register_1_q2, shift_register_1_q3, shift_register_1_q4);
  nand nand_2 (nand_2_out, shift_register_1_q5, shift_register_1_q6, shift_register_1_q7, shift_register_1_q8, shift_register_1_q9);
  or or_1 (or_1_out, V, G);
  Shift_Register #(.length(10)) shift_register_1 (
    .in(R), .clk(CkL), .q0(shift_register_1_q0), .q1(shift_register_1_q1), .q2(shift_register_1_q2),
    .q3(shift_register_1_q3), .q4(shift_register_1_q4), .q5(shift_register_1_q5), .q6(shift_register_1_q6),
    .q7(shift_register_1_q7), .q8(shift_register_1_q8), .q9(shift_register_1_q9));  // open: shift, out, load, clr, d0, d1, d2, d3, d4, d5, d6, d7, d8, d9
  D_Flip_Flop d_ff_1 (.clk(CkL), .D(or_1_out), .Q(RS), .preset(or_1_out), .reset(not_1_out));  // open: Qn, en
  not not_1 (not_1_out, or_1_out);

  // Other names for the same wires on the sheet: S = VS; SegnaleR = RS

  // Notes on the sheet:
  //   Semaforo originale
  //   Gestione rosso speculare
  //   CIRCUITO PER IL FUNZIONAMENTO DEI SEMAFORI 3 E 4
  //   (SPECULARE ALL'ORIGINALE)
  //   Gestione verde e giallo speculari
endmodule

module Multa (
  input  _1,
  input  CkL,
  input  _2,
  input  _3,
  input  _4,
  output [3:0] D,
  output [3:0] U,
  output I
);

  wire and_1_out, and_2_out, and_3_out, and_4_out, and_5_out, counter_1_carry, R, RS, S1;

  Semaforo semaforo_1 (.R(R), .CkL(CkL));  // open: V, G
  SemaforoSpeculare semaforospeculare_1 (.CkL(CkL), .RS(RS));  // open: VS, GS
  or or_1 (I, and_1_out, and_2_out, and_3_out, and_4_out);
  and and_1 (and_1_out, _1, R);
  and and_2 (and_2_out, _2, R);
  and and_3 (and_3_out, _3, RS);
  and and_4 (and_4_out, _4, RS);
  Counter #(.width(4), .max('ha)) counter_1 (
    .Q(D), .carry(counter_1_carry), .clk(and_5_out), .clr(counter_1_carry));  // open: load, D, count
  and and_5 (and_5_out, I, S1);
  Counter #(.width(4), .max('ha)) counter_2 (.Q(U), .carry(S1), .clk(I), .clr(S1));  // open: load, D, count

  // Notes on the sheet:
  //   Semafori per riportare il segnale di semaforo rosso
  //   Circuito che alla pressione del bottone fa "scattare" la multa
  //   CIRCUITO PER IL CONTATORE DI MULTE E PER IL FUNZIONAMENTO DEL SEGNALE I DI "PASSAGGIO CON IL ROSSO"
  //   Contatore di multe decine/unità
endmodule

module TargaRandom (
  input  Ck,
  input  _1,
  input  _2,
  input  CkL,
  input  _3,
  input  _4,
  output [3:0] N1,
  output [3:0] N2,
  output [3:0] N3,
  output [3:0] N4,
  output [3:0] N5,
  output [3:0] N6,
  output [3:0] N7
);

  wire I;

  Multa multa_1 (._1(_1), ._2(_2), ._3(_3), ._4(_4), .CkL(CkL), .I(I));  // open: D, U
  Random #(.width(4), .seed(10)) random_1 (.clk(Ck), .next(I), .out(N1));  // open: clr
  Random #(.width(4), .seed(12)) random_2 (.clk(Ck), .next(I), .out(N2));  // open: clr
  Random #(.width(4), .seed(3)) random_3 (.clk(Ck), .next(I), .out(N3));  // open: clr
  Random #(.width(4), .seed(2)) random_4 (.clk(Ck), .next(I), .out(N4));  // open: clr
  Random #(.width(4), .seed(8)) random_5 (.clk(Ck), .next(I), .out(N5));  // open: clr
  Random #(.width(4), .seed(15)) random_6 (.clk(Ck), .next(I), .out(N6));  // open: clr
  Random #(.width(4), .seed(14)) random_7 (.clk(Ck), .next(I), .out(N7));  // open: clr

  // Notes on the sheet:
  //   Circuito multe riutilizzato per input I.
  //   lavorare inutilmente i random generator.
  //   Omettibile in quanto l'input non passa in memoria, inserito per evitare di far 
  //   GENERATORE TARGA PSEUDO-CASUALE
  //   una cifra alfa numerica della targa.
  //   Ogni modulo genera in maniera pseudo-casuale i 4 bit che compongono
endmodule

module Orologio (
  input  CkL,
  input  Reset,
  input  M_plus,
  input  H_plus,
  output [3:0] Secondi_1,
  output [3:0] Secondi_2,
  output [3:0] Minuti_1,
  output [3:0] Minuti_2,
  output [3:0] Ore_1,
  output [3:0] Ore_2
);

  wire and_1_out, and_2_out, and_3_out, and_4_out, and_5_out, and_6_out, and_7_out, and_8_out, and_9_out,
       or_1_out, or_2_out, or_3_out, or_4_out, or_5_out, or_6_out, or_7_out, or_8_out;

  Counter #(.width(4), .max('hf)) counter_1 (
    .Q(Secondi_1), .clk(and_1_out), .clr(or_1_out));  // open: load, D, count, carry
  and and_1 (and_1_out, CkL, ~Reset);  // AND_Gate
  or or_1 (or_1_out, and_2_out, Reset);
  and and_2 (and_2_out, ~Secondi_1[0], Secondi_1[1], ~Secondi_1[2], Secondi_1[3]);  // AND_Gate
  Counter #(.width(4), .max('hf)) counter_2 (
    .Q(Secondi_2), .clk(or_1_out), .clr(or_2_out));  // open: load, D, count, carry
  or or_2 (or_2_out, and_3_out, Reset);
  or or_3 (or_3_out, or_2_out, M_plus);
  and and_3 (and_3_out, ~Secondi_2[0], Secondi_2[1], Secondi_2[2], ~Secondi_2[3]);  // AND_Gate
  Counter #(.width(4), .max('hf)) counter_3 (
    .Q(Minuti_1), .clk(or_3_out), .clr(or_4_out));  // open: load, D, count, carry
  and and_4 (and_4_out, ~Minuti_1[0], Minuti_1[1], ~Minuti_1[2], Minuti_1[3]);  // AND_Gate
  or or_4 (or_4_out, and_4_out, Reset);
  or or_5 (or_5_out, or_7_out, H_plus);
  or or_6 (or_6_out, and_7_out, and_6_out, Reset);
  Counter #(.width(4), .max('hf)) counter_4 (
    .Q(Minuti_2), .clk(or_4_out), .clr(or_7_out));  // open: load, D, count, carry
  and and_5 (and_5_out, ~Minuti_2[0], Minuti_2[1], Minuti_2[2], ~Minuti_2[3]);  // AND_Gate
  or or_7 (or_7_out, and_5_out, Reset);
  Counter #(.width(4), .max('hf)) counter_5 (.Q(Ore_1), .clk(or_5_out), .clr(or_6_out));  // open: load, D, count, carry
  and and_6 (and_6_out, and_8_out, Ore_2[1]);
  and and_7 (and_7_out, ~Ore_1[0], Ore_1[1], ~Ore_1[2], Ore_1[3]);  // AND_Gate
  and and_8 (and_8_out, ~Ore_1[0], ~Ore_1[1], Ore_1[2], ~Ore_1[3]);  // AND_Gate
  Counter #(.width(4), .max('hf)) counter_6 (.Q(Ore_2), .clk(or_6_out), .clr(or_8_out));  // open: load, D, count, carry
  and and_9 (and_9_out, Ore_2[0], Ore_2[1], ~Ore_2[2], ~Ore_2[3]);  // AND_Gate
  or or_8 (or_8_out, and_9_out, Reset);

  // Notes on the sheet:
  //   Aggiunge 1 minuto
  //   Aggiunge 1 ora
  //   OROLOGIO
endmodule

module MemTarghe (
  input  Ck,
  input  CkL,
  input  _1,
  input  _2,
  input  _3,
  input  _4,
  output [3:0] P1,
  output [3:0] S1,
  output [3:0] T1,
  output [3:0] P2,
  output [3:0] S2,
  output [3:0] T2,
  output [3:0] P3,
  output [3:0] S3,
  output [3:0] T3,
  output [3:0] P4,
  output [3:0] S4,
  output [3:0] T4,
  output [3:0] P5,
  output [3:0] S5,
  output [3:0] T5,
  output [3:0] P6,
  output [3:0] S6,
  output [3:0] T6,
  output [3:0] P7,
  output [3:0] S7,
  output [3:0] T7
);

  wire I;
  wire [3:0] targarandom_1_n1, targarandom_1_n2, targarandom_1_n3, targarandom_1_n4, targarandom_1_n5,
       targarandom_1_n6, targarandom_1_n7;

  Multa multa_1 (._1(_1), ._2(_2), ._3(_3), ._4(_4), .CkL(CkL), .I(I));  // open: D, U
  TargaRandom targarandom_1 (
    .N1(targarandom_1_n1), .N2(targarandom_1_n2), .N3(targarandom_1_n3), .N4(targarandom_1_n4),
    .N5(targarandom_1_n5), .N6(targarandom_1_n6), .N7(targarandom_1_n7), ._1(_1), ._2(_2), ._3(_3), ._4(_4),
    .CkL(CkL), .Ck(Ck));
  Register #(.width(4)) register_1 (.D(targarandom_1_n1), .en(I), .Q(P1), .clk(Ck));  // open: clr
  Register #(.width(4)) register_2 (.D(targarandom_1_n2), .en(I), .Q(P2), .clk(Ck));  // open: clr
  Register #(.width(4)) register_3 (.D(targarandom_1_n3), .en(I), .Q(P3), .clk(Ck));  // open: clr
  Register #(.width(4)) register_4 (.D(targarandom_1_n4), .en(I), .Q(P4), .clk(Ck));  // open: clr
  Register #(.width(4)) register_5 (.D(targarandom_1_n5), .en(I), .Q(P5), .clk(Ck));  // open: clr
  Register #(.width(4)) register_6 (.D(targarandom_1_n6), .en(I), .Q(P6), .clk(Ck));  // open: clr
  Register #(.width(4)) register_7 (.D(targarandom_1_n7), .en(I), .Q(P7), .clk(Ck));  // open: clr
  Register #(.width(4)) register_8 (.D(P1), .en(I), .Q(S1), .clk(Ck));  // open: clr
  Register #(.width(4)) register_9 (.D(P2), .en(I), .Q(S2), .clk(Ck));  // open: clr
  Register #(.width(4)) register_10 (.D(P3), .en(I), .Q(S3), .clk(Ck));  // open: clr
  Register #(.width(4)) register_11 (.D(P4), .en(I), .Q(S4), .clk(Ck));  // open: clr
  Register #(.width(4)) register_12 (.D(P5), .en(I), .Q(S5), .clk(Ck));  // open: clr
  Register #(.width(4)) register_13 (.D(P6), .en(I), .Q(S6), .clk(Ck));  // open: clr
  Register #(.width(4)) register_14 (.D(P7), .en(I), .Q(S7), .clk(Ck));  // open: clr
  Register #(.width(4)) register_15 (.D(S1), .en(I), .Q(T1), .clk(Ck));  // open: clr
  Register #(.width(4)) register_16 (.D(S2), .en(I), .Q(T2), .clk(Ck));  // open: clr
  Register #(.width(4)) register_17 (.D(S3), .en(I), .Q(T3), .clk(Ck));  // open: clr
  Register #(.width(4)) register_18 (.D(S4), .en(I), .Q(T4), .clk(Ck));  // open: clr
  Register #(.width(4)) register_19 (.D(S5), .en(I), .Q(T5), .clk(Ck));  // open: clr
  Register #(.width(4)) register_20 (.D(S6), .en(I), .Q(T6), .clk(Ck));  // open: clr
  Register #(.width(4)) register_21 (.D(S7), .en(I), .Q(T7), .clk(Ck));  // open: clr

  // Notes on the sheet:
  //   Circuito multa, riportato per utilizzare input I
  //   Circuito per la memorizzazione delle ultime 3 targhe
  //   MEMORIA TARGHE MULTE
  //   Prima
  //   Seconda
  //   Terza
endmodule

module MemOrologio (
  input  Ck,
  input  CkL,
  input  Reset,
  input  M_plus,
  input  H_plus,
  input  _1,
  input  _2,
  input  _3,
  input  _4,
  output [3:0] P1,
  output [3:0] S1,
  output [3:0] T1,
  output [3:0] P2,
  output [3:0] S2,
  output [3:0] T2,
  output [3:0] P3,
  output [3:0] S3,
  output [3:0] T3,
  output [3:0] P4,
  output [3:0] S4,
  output [3:0] T4,
  output [3:0] P5,
  output [3:0] S5,
  output [3:0] T5,
  output [3:0] P6,
  output [3:0] S6,
  output [3:0] T6
);

  wire I;
  wire [3:0] orologio_1_minuti_1, orologio_1_minuti_2, orologio_1_ore_1, orologio_1_ore_2,
       orologio_1_secondi_1, orologio_1_secondi_2;

  Multa multa_1 (._1(_1), ._2(_2), ._3(_3), ._4(_4), .CkL(CkL), .I(I));  // open: D, U
  Orologio orologio_1 (
    .CkL(CkL), .Reset(Reset), .M_plus(M_plus), .H_plus(H_plus), .Secondi_1(orologio_1_secondi_1),
    .Secondi_2(orologio_1_secondi_2), .Minuti_1(orologio_1_minuti_1), .Minuti_2(orologio_1_minuti_2),
    .Ore_1(orologio_1_ore_1), .Ore_2(orologio_1_ore_2));
  Register #(.width(4)) register_1 (.D(orologio_1_ore_2), .en(I), .Q(P1), .clk(Ck));  // open: clr
  Register #(.width(4)) register_2 (.D(orologio_1_ore_1), .en(I), .Q(P2), .clk(Ck));  // open: clr
  Register #(.width(4)) register_3 (.D(orologio_1_minuti_2), .en(I), .Q(P3), .clk(Ck));  // open: clr
  Register #(.width(4)) register_4 (.D(orologio_1_minuti_1), .en(I), .Q(P4), .clk(Ck));  // open: clr
  Register #(.width(4)) register_5 (.D(orologio_1_secondi_2), .en(I), .Q(P5), .clk(Ck));  // open: clr
  Register #(.width(4)) register_6 (.D(orologio_1_secondi_1), .en(I), .Q(P6), .clk(Ck));  // open: clr
  Register #(.width(4)) register_7 (.D(P1), .en(I), .Q(S1), .clk(Ck));  // open: clr
  Register #(.width(4)) register_8 (.D(P2), .en(I), .Q(S2), .clk(Ck));  // open: clr
  Register #(.width(4)) register_9 (.D(P3), .en(I), .Q(S3), .clk(Ck));  // open: clr
  Register #(.width(4)) register_10 (.D(P4), .en(I), .Q(S4), .clk(Ck));  // open: clr
  Register #(.width(4)) register_11 (.D(P5), .en(I), .Q(S5), .clk(Ck));  // open: clr
  Register #(.width(4)) register_12 (.D(P6), .en(I), .Q(S6), .clk(Ck));  // open: clr
  Register #(.width(4)) register_13 (.D(S1), .en(I), .Q(T1), .clk(Ck));  // open: clr
  Register #(.width(4)) register_14 (.D(S2), .en(I), .Q(T2), .clk(Ck));  // open: clr
  Register #(.width(4)) register_15 (.D(S3), .en(I), .Q(T3), .clk(Ck));  // open: clr
  Register #(.width(4)) register_16 (.D(S4), .en(I), .Q(T4), .clk(Ck));  // open: clr
  Register #(.width(4)) register_17 (.D(S5), .en(I), .Q(T5), .clk(Ck));  // open: clr
  Register #(.width(4)) register_18 (.D(S6), .en(I), .Q(T6), .clk(Ck));  // open: clr

  // Other names for the same wires on the sheet: PO1[3:0] = P1; PO2[3:0] = P2; PO3[3:0] = P3; PO4[3:0] = P4;
  //   PO5[3:0] = P5; PO6[3:0] = P6; SO1[3:0] = S1; SO2[3:0] = S2; SO3[3:0] = S3; SO4[3:0] = S4; SO5[3:0] = S5;
  //   SO6[3:0] = S6; TO1[3:0] = T1; TO2[3:0] = T2; TO3[3:0] = T3; TO4[3:0] = T4; TO5[3:0] = T5; TO6[3:0] = T6

  // Notes on the sheet:
  //   Circuito multa, riportato per utilizzare input I
  //   MEMORIA ORARI MULTE
  //   Circuito per la memorizzazione degli ultimi 3 orari
  //   Primo
  //   Secondo
  //   Terzo
endmodule
